# Fritzing sketch ButtonSketch (saved by Fritzing 0.9.1b)
breadboards: 1

parts:
  S1 = Pushbutton [package="[THT]"]
  Part1 = Arduino Pro Mini v13

nets:
  N1: S1.Pin_1, S1.Pin_2, Part1.D4
  N2: S1.Pin_3, S1.Pin_4, Part1.GND
