# Fritzing sketch TwoButtonSketch (saved by Fritzing 0.9.1b)
breadboards: 1

parts:
  S1 = Pushbutton [package="[THT]"]
  Part1 = Arduino Pro Mini v13
  S2 = Pushbutton [package="[THT]"]

nets:
  N1: S1.Pin_1, S1.Pin_2, Part1.D4
  N2: S1.Pin_3, S1.Pin_4, Part1.GND, S2.Pin_3, S2.Pin_4
  N3: Part1.D7, S2.Pin_1, S2.Pin_2
